# Fritzing sketch handheld (saved by Fritzing 1.0.6)
breadboards: 2

parts:
  Part2 = Adafruit Feather RP2040 RFM [part_number="Adafruit #5712"]
  Part3 = Adafruit PA1010D Mini GPS Module [part_number="Adafruit #4415"]
  Part4 = Lithium Ion Polymer Battery 3.7v 2500mAh [part_number=328]
  U1 = SWITCH_SPDT [package=kps-1290]
  2_7"_(PID_4694) = SHARP Memory Display 1.3 inch 96x96 [part_number=1393]
  Chirp = Momentary Switch [package=ksa_sealed_tac_switch]
  ARM = Momentary Switch [package=ksa_sealed_tac_switch]
  Cycle_View = Momentary Switch [package=ksa_sealed_tac_switch]

nets:
  GND: Part2.GND, Part3.GND, Part4.negative, 2_7"_(PID_4694).GND, Chirp.2, ARM.2, Cycle_View.2
  +3V3: Part2.+3V3, Part3.VCC, 2_7"_(PID_4694).3.3V
  N1: Part2.SDA, Part3.SDA
  N2: Part2.SCL, Part3.SCL
  N3: Part2.MOSI, 2_7"_(PID_4694).DISP
  N4: Part2.SCK, 2_7"_(PID_4694).SCLK
  N5: Part2.VBAT, U1.O, Chirp.4, ARM.4, Cycle_View.4
  N6: Part2.D11, Cycle_View.3
  N7: Part2.D10, ARM.3
  N8: Part2.D9, Chirp.3
  N9: Part2.D6, 2_7"_(PID_4694).CS
  N10: Part4.positive, U1.P

custom parts:
  Adafruit Feather RP2040 RFM: This is the Adafruit Feather RP2040 RFM. We call these RadioFruits, our take on an microcontroller with packet radio transceiver with built-in USB and battery charging. It's an Adafruit Feather RP2040 with a radio module cooked in! Great for making wireless networks that are more flexible than Bluetooth LE and without the high power requirements of WiFi. Feather is the development board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
  Adafruit PA1010D Mini GPS Module: This miniature GPS breakout is only 1" x 1" (~ 25mm x 25mm) but houses a complete GPS/GNSS solution with both I2C and UART interfaces. There's even an antenna on top so it's plug and play! Support for GPS, GLONASS, GALILEO, QZSS -165 dBm sensitivity, up to 10 Hz updates Up to 210 PRN channels with 99 search channels and 33 simultaneous tracking channels 5V friendly design and only 30mA current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
  Lithium Ion Polymer Battery 3.7v 2500mAh: Lithium ion polymer (also known as 'lipo' or 'lipoly') batteries are thin, light and powerful. The output ranges from 4.2V when completely charged to 3.7V. This battery has a capacity of 2500mAh for a total of about 10 Wh. The batteries come pre-attached with a genuine 2-pin JST-PH connector as shown and include the necessary protection circuitry.
  SHARP Memory Display 1.3 inch 96x96: The 1.3" SHARP Memory LCD display is a cross between an eInk (e-paper) display and an LCD. It has the ultra-low power usage of eInk and the fast-refresh rates of an LCD. This model has a matt silver background, and pixels show up as little mirrors for a silver-reflective display, a really beautiful and unique look. It does not have a backlight, but it is daylight readable. For dark/night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
