# Fritzing sketch payload (saved by Fritzing 1.0.6)
breadboards: 1

parts:
  Part1 = Adafruit Feather RP2040 RFM [part_number="Adafruit #5712"]
  Adafruit_BMP580_Temperature_and_Pressure_Sensor1 = Adafruit BMP580 Temperature and Pressure Sensor [part_number=#6411]
  Part2 = Adafruit PA1010D Mini GPS Module [part_number="Adafruit #4415"]
  Part3 = Adafruit Precision 9-DoF LIS3MDL + LSM6DSOX [part_number="Adafruit #4517"]
  J1 = Piezo Speaker
  Part4 = Lithium Ion Polymer Battery 3.7v 500mAh [part_number=1578]
  U1 = SWITCH_SPDT [package=kps-1290]

nets:
  GND: Part1.GND, Part1.SDA, Adafruit_BMP580_Temperature_and_Pressure_Sensor1.GND, Adafruit_BMP580_Temperature_and_Pressure_Sensor1.SDI/SDA, Part2.GND, Part2.SDA, Part3.GND, Part3.SDA, Part4.negative
  VCC: Part1.+3V3, Adafruit_BMP580_Temperature_and_Pressure_Sensor1.VCC, Part2.VCC, Part3.VCC
  N1: Part1.SCL, Adafruit_BMP580_Temperature_and_Pressure_Sensor1.SCK/SCL, Part2.SCL, Part3.SCL
  N2: Part1.VBAT, U1.O
  N3: Part1.D6, J1.pin1
  N4: Part1.D5, J1.pin2
  N5: Part4.positive, U1.P

custom parts:
  Adafruit Feather RP2040 RFM: This is the Adafruit Feather RP2040 RFM. We call these RadioFruits, our take on an microcontroller with packet radio transceiver with built-in USB and battery charging. It's an Adafruit Feather RP2040 with a radio module cooked in! Great for making wireless networks that are more flexible than Bluetooth LE and without the high power requirements of WiFi. Feather is the development board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
  Adafruit BMP580 Temperature and Pressure Sensor: Bosch has been a leader in barometric pressure sensors, from the BMP085. BMP180, BMP280, BMP388, BMP390... now we've got the next generation, the Adafruit BMP580 Precision Barometric Pressure and Altimeter Breakout. It can even be used in either I2C and SPI configurations. The BMP580 is the next-generation of sensors from Bosch and is the upgrade to the BMP2xx and BMP3xx - with a low-altitude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
  Adafruit PA1010D Mini GPS Module: This miniature GPS breakout is only 1" x 1" (~ 25mm x 25mm) but houses a complete GPS/GNSS solution with both I2C and UART interfaces. There's even an antenna on top so it's plug and play! Support for GPS, GLONASS, GALILEO, QZSS -165 dBm sensitivity, up to 10 Hz updates Up to 210 PRN channels with 99 search channels and 33 simultaneous tracking channels 5V friendly design and only 30mA current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
  Adafruit Precision 9-DoF LIS3MDL + LSM6DSOX: Add high quality motion, direction and orientation sensing to your Arduino project with this all-in-one 9 Degree of Freedom (9-DoF) sensor with sensors from ST. This little breakout contains two chips that sit side-by-side to provide 9 degrees of full-motion data. The board includes an LSM6DSOX, a 6-DoF IMU accelerometer + gyro. The 3-axis accelerometer can tell you which direction is down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
  Lithium Ion Polymer Battery 3.7v 500mAh: Lithium ion polymer (also known as 'lipo' or 'lipoly') batteries are thin, light and powerful. The output ranges from 4.2V when completely charged to 3.7V. This battery has a capacity of 500mAh for a total of about 1.9 Wh. The batteries come pre-attached with a genuine 2-pin JST-PH connector as shown and include the necessary protection circuitry.
